# Fritzing sketch CAGAMPANG-PERPETUA-MACABUDBUD-MOZO (saved by Fritzing 0.9.3b)
perfboards: 1

parts:
  Matrix_keypad1 = KEYPAD 4x4
  Part1 = Arduino Mega 2560 (Rev3)
  LED1 = LED - 5mm [color="Red (633nm)" package="5 mm [THT]"]
  LED2 = LED - 5mm [color="Red (633nm)" package="5 mm [THT]"]
  LED3 = LED - 5mm [color="Red (633nm)" package="5 mm [THT]"]
  LED4 = LED - 5mm [color="Red (633nm)" package="5 mm [THT]"]
  LED5 = LED - 5mm [color="Red (633nm)" package="5 mm [THT]"]
  LED6 = LED - 5mm [color="Red (633nm)" package="5 mm [THT]"]
  LED7 = LED - 5mm [color="Red (633nm)" package="5 mm [THT]"]
  LED8 = LED - 5mm [color="Red (633nm)" package="5 mm [THT]"]
  LED9 = LED - 5mm [color="Red (633nm)" package="5 mm [THT]"]
  LED10 = LED - 5mm [color="Red (633nm)" package="5 mm [THT]"]
  LED11 = LED - 5mm [color="Red (633nm)" package="5 mm [THT]"]
  LED12 = LED - 5mm [color="Red (633nm)" package="5 mm [THT]"]
  LED13 = LED - 5mm [color="Red (633nm)" package="5 mm [THT]"]
  LED14 = LED - 5mm [color="Red (633nm)" package="5 mm [THT]"]
  LED15 = LED - 5mm [color="Red (633nm)" package="5 mm [THT]"]
  LED16 = LED - 5mm [color="Red (633nm)" package="5 mm [THT]"]
  LED17 = LED - 5mm [color="Red (633nm)" package="5 mm [THT]"]
  LED18 = LED - 5mm [color="Red (633nm)" package="5 mm [THT]"]
  LED19 = LED - 5mm [color="Red (633nm)" package="5 mm [THT]"]
  LED20 = LED - 5mm [color="Red (633nm)" package="5 mm [THT]"]
  LED21 = LED - 5mm [color="Red (633nm)" package="5 mm [THT]"]
  LED22 = LED - 5mm [color="Red (633nm)" package="5 mm [THT]"]
  LED23 = LED - 5mm [color="Red (633nm)" package="5 mm [THT]"]
  LED24 = LED - 5mm [color="Red (633nm)" package="5 mm [THT]"]
  LED25 = LED - 5mm [color="Red (633nm)" package="5 mm [THT]"]

nets:
  N1: Matrix_keypad1.col1, Part1.D6_PWM
  N2: Matrix_keypad1.col2, Part1.D7_PWM
  N3: Matrix_keypad1.col3, Part1.D8_PWM
  N4: Matrix_keypad1.col4, Part1.D9_PWM
  N5: Matrix_keypad1.row1, Part1.D2_PWM
  N6: Matrix_keypad1.row2, Part1.D3_PWM
  N7: Matrix_keypad1.row3, Part1.D4_PWM
  N8: Matrix_keypad1.row4, Part1.D5_PWM
  N9: Part1.GND, LED1.cathode, LED2.cathode, LED3.cathode, LED4.cathode, LED5.cathode, LED6.cathode, LED7.cathode, LED8.cathode, LED9.cathode, LED10.cathode, LED11.cathode, LED12.cathode, LED13.cathode, LED14.cathode, LED15.cathode, LED16.cathode, LED17.cathode, LED18.cathode, LED19.cathode, LED20.cathode, LED21.cathode, LED22.cathode, LED23.cathode, LED24.cathode, LED25.cathode
  N10: Part1.D26, LED1.anode
  N11: Part1.D27, LED2.anode
  N12: Part1.D28, LED3.anode
  N13: Part1.D29, LED4.anode
  N14: Part1.D30, LED5.anode
  N15: Part1.D31, LED6.anode
  N16: Part1.D32, LED7.anode
  N17: Part1.D33, LED8.anode
  N18: Part1.D34, LED9.anode
  N19: Part1.D35, LED10.anode
  N20: Part1.D36, LED11.anode
  N21: Part1.D37, LED12.anode
  N22: Part1.D38, LED13.anode
  N23: Part1.D39, LED14.anode
  N24: Part1.D40, LED15.anode
  N25: Part1.D41, LED16.anode
  N26: Part1.D42, LED17.anode
  N27: Part1.D43, LED18.anode
  N28: Part1.D44, LED19.anode
  N29: Part1.D45, LED20.anode
  N30: Part1.D46, LED21.anode
  N31: Part1.D47, LED22.anode
  N32: Part1.D48, LED23.anode
  N33: Part1.D49, LED24.anode
  N34: Part1.D50, LED25.anode

custom parts:
  KEYPAD 4x4: Matrix keypad 16 buttons, 4 rows x 4 columns
